# Fritzing sketch CircuitDiagram (saved by Fritzing 0.9.3b)

parts:
  Part1 = Arduino Nano (Rev3.0)
  U1 = POT [package=alps_pot]
  U2 = POT [package=alps_pot]
  S1 = Pushbutton [package="[THT]"]
  S2 = Pushbutton [package="[THT]"]
  S3 = Pushbutton [package="[THT]"]
  R1 = Resistor [tolerance=±5% resistance=10k package=THT]
  R2 = Resistor [tolerance=±5% resistance=10k package=THT]
  R3 = Resistor [tolerance=±5% resistance=10k package=THT]
  Part2 = Ludus ProtoShield
  VCC1 = Battery
  VCC2 = Battery
  J1 = Basic Servo
  J2 = Basic Servo
  J3 = Basic Servo
  LED13 = LED - 5mm [color="Red (633nm)" package="5 mm [THT]"]
  LED14 = LED - 5mm [color="Red (633nm)" package="5 mm [THT]"]
  LED15 = LED - 5mm [color="Red (633nm)" package="5 mm [THT]"]
  R10 = Resistor [tolerance=±5% resistance=220 package=THT]
  R11 = Resistor [tolerance=±5% resistance=220 package=THT]
  R12 = Resistor [tolerance=±5% resistance=220 package=THT]
  S4 = Pushbutton [package="[THT]"]
  R13 = Resistor [tolerance=±5% resistance=10k package=THT]
  LED16 = LED - 5mm [color="White (6500K)" package="5 mm [THT]"]  # not connected
  LED17 = LED - 5mm [color="White (6500K)" package="5 mm [THT]"]  # not connected
  R14 = Resistor [tolerance=±5% resistance=150 package=THT]  # not connected
  U3 = 74HC595 [package="DIP16 [THT]"]  # not connected

nets:
  GND: Part1.GND, U1.E, U2.E, R1.Pin_0, R2.Pin_0, R3.Pin_0, Part2.GND, J1.gnd, J2.gnd, J3.gnd, R10.Pin_1, R11.Pin_1, R12.Pin_1, R13.Pin_0
  N1: Part1.D2, S1.Pin_1, S1.Pin_2, R3.Pin_1
  N2: Part1.D3, S2.Pin_1, S2.Pin_2, R2.Pin_1
  N3: Part1.D4, S3.Pin_1, S3.Pin_2, R1.Pin_1
  N4: Part1.D5, S4.Pin_1, S4.Pin_2, R13.Pin_1
  N5: Part1.D8, LED15.anode
  N6: Part1.D9, LED14.anode
  N7: Part1.D10, LED13.anode
  5V: Part1.5V, U1.A, U2.A, S1.Pin_3, S1.Pin_4, S2.Pin_3, S2.Pin_4, S3.Pin_3, S3.Pin_4, Part2.VCC, S4.Pin_3, S4.Pin_4
  N8: Part1.A5, Part2.SCL
  N9: Part1.A4, Part2.SDA
  N10: Part1.A1, U1.S
  N11: Part1.A0, U2.S
  VCC: Part2.ANALOG_PWR_RAIL, J1.vcc, J2.vcc, J3.vcc
  N12: Part2.A0, J1.pulse
  N13: Part2.A1, J2.pulse
  N14: Part2.A2, J3.pulse
  N15: Part2.AOUT2, VCC1.-
  N16: Part2.AOUT1, VCC2.+
  N17: VCC1.+, VCC2.-

notes:
  light, switch
  cont
  light
  save, load
  pretend this is PCA9685 16-Channel Servo Driver
  6v ~2000mAh
  mode leds
  Pins:
  5+
  GND
  A0
  A1
  A2
